# Fritzing sketch _Analogue keyboard (saved by Fritzing 1.0.7)
breadboards: 1
stripboards: 3

parts:
  S1 = Momentary Switch [package=ksa_sealed_tac_switch]
  S2 = Momentary Switch [package=ksa_sealed_tac_switch]
  S3 = Momentary Switch [package=ksa_sealed_tac_switch]
  R1 = Resistor [tolerance=±5% resistance=2.2k package="2010 [SMD]"]
  R2 = Resistor [tolerance=±5% resistance=1k package="2010 [SMD]"]
  R3 = Resistor [tolerance=±5% resistance=1k package="2010 [SMD]"]
  R4 = Resistor [tolerance=±5% resistance=1k package="2010 [SMD]"]
  S4 = Momentary Switch [package=ksa_sealed_tac_switch]
  S5 = Momentary Switch [package=ksa_sealed_tac_switch]
  S6 = Momentary Switch [package=ksa_sealed_tac_switch]
  S7 = Momentary Switch [package=ksa_sealed_tac_switch]
  R5 = Resistor [tolerance=±5% resistance=1k package="2010 [SMD]"]
  R6 = Resistor [tolerance=±5% resistance=1k package="2010 [SMD]"]
  R7 = Resistor [tolerance=±5% resistance=1k package="2010 [SMD]"]
  J4 = male pin header, 3 pins [form="♂ (male)"]
  J6 = male pin header, 3 pins [form="♂ (male)"]
  R11 = Resistor [tolerance=±5% resistance=2.2k package="2010 [SMD]"]
  R12 = Resistor [tolerance=±5% resistance=1k package="2010 [SMD]"]
  J7 = male pin header, 3 pins [form="♂ (male)"]
  J8 = male pin header, 3 pins [form="♂ (male)"]
  J10 = male pin header, 3 pins [form="♂ (male)"]
  J11 = male pin header, 3 pins [form="♂ (male)"]
  J13 = male pin header, 3 pins [form="♂ (male)"]
  R18 = Resistor [tolerance=±5% resistance=1k package="2010 [SMD]"]
  R19 = Resistor [tolerance=±5% resistance=1k package="2010 [SMD]"]
  R20 = Resistor [tolerance=±5% resistance=1k package="2010 [SMD]"]
  R21 = Resistor [tolerance=±5% resistance=1k package="2010 [SMD]"]
  J14 = male pin header, 3 pins [form="♂ (male)"]
  S8 = Momentary Switch [package=ksa_sealed_tac_switch]  # not connected
  S9 = Momentary Switch [package=ksa_sealed_tac_switch]  # not connected
  J15 = male pin header, 3 pins [form="♂ (male)"]
  S10 = Momentary Switch [package=ksa_sealed_tac_switch]  # not connected
  J16 = male pin header, 3 pins [form="♂ (male)"]
  S11 = Momentary Switch [package=ksa_sealed_tac_switch]  # not connected
  J17 = male pin header, 3 pins [form="♂ (male)"]
  S12 = Momentary Switch [package=ksa_sealed_tac_switch]  # not connected
  J18 = male pin header, 3 pins [form="♂ (male)"]
  S13 = Momentary Switch [package=ksa_sealed_tac_switch]  # not connected
  J19 = male pin header, 3 pins [form="♂ (male)"]
  S29 = Momentary Switch [package=ksa_sealed_tac_switch]
  S30 = Momentary Switch [package=ksa_sealed_tac_switch]
  S31 = Momentary Switch [package=ksa_sealed_tac_switch]
  S32 = Momentary Switch [package=ksa_sealed_tac_switch]
  S33 = Momentary Switch [package=ksa_sealed_tac_switch]
  R33 = Resistor [tolerance=±5% resistance=2.2k package="2010 [SMD]"]
  J29 = male pin header, 3 pins [form="♂ (male)"]
  R34 = Resistor [tolerance=±5% resistance=1k package="2010 [SMD]"]
  R35 = Resistor [tolerance=±5% resistance=1k package="2010 [SMD]"]
  R36 = Resistor [tolerance=±5% resistance=1k package="2010 [SMD]"]
  R37 = Resistor [tolerance=±5% resistance=1k package="2010 [SMD]"]

nets:
  N1: S1.1, S2.1, S3.1, S4.1, S5.1, S6.1, S7.1
  N2: S1.3, R1.Pin_1, R2.Pin_0
  N3: S2.3, R2.Pin_1, R3.Pin_0
  N4: S3.3, R3.Pin_1, R4.Pin_0
  N5: R4.Pin_1, S4.3, R5.Pin_0
  N6: S5.3, R5.Pin_1, R6.Pin_0
  N7: S6.3, R6.Pin_1, R7.Pin_0
  N8: S7.3, R7.Pin_1
  N9: J4.pin1, J6.pin1, R11.Pin_0, R21.Pin_0, J14.pin3
  N10: J4.pin2, J4.pin3, J6.pin2, J6.pin3, R11.Pin_1, J7.pin2, J7.pin3, J8.pin2, J8.pin3, J10.pin2, J10.pin3, J11.pin2, J11.pin3, J13.pin2, J13.pin3, J14.pin1, J15.pin1, J16.pin1, J17.pin1, J18.pin1, J19.pin1
  N11: R12.Pin_0, J7.pin1, R21.Pin_1, J15.pin3
  N12: R12.Pin_1, J10.pin1, R18.Pin_0, J16.pin3
  N13: J8.pin1, R20.Pin_1, J19.pin3
  N14: J11.pin1, R18.Pin_1, R19.Pin_0, J17.pin3
  N15: J13.pin1, R19.Pin_1, R20.Pin_0, J18.pin3
  N16: S29.1, S29.2, S30.1, S30.2, S31.1, S31.2, S32.1, S32.2, S33.1, S33.2, J29.pin3
  N17: S29.3, S29.4, R35.Pin_1
  N18: S30.4, R34.Pin_0, R37.Pin_1
  N19: S31.4, R33.Pin_0, J29.pin1, R37.Pin_0
  N20: S32.4, R35.Pin_0, R36.Pin_1
  N21: S33.4, R34.Pin_1, R36.Pin_0
  N22: R33.Pin_1, J29.pin2

notes:
  Microbit P0
  When no buttons pressed reads approx 1023. Button 1=0, button 2=44, button3=84, button4=121, button5=156, button6=188 etc
  Pull-up 22k
  BML version for BML standard buttons
  Ladder 1k
  BML version for with build in small buttons
  Break tracks like this:
